# Fritzing sketch knock2 (saved by Fritzing 0.9.3b)
breadboards: 1

parts:
  WeMos_D1_Mini1 = WeMos D1 Mini
  U1 = ADXL335 [package=lfcsp-16]

nets:
  N1: WeMos_D1_Mini1.3V3, U1.VS
  N2: WeMos_D1_Mini1.A0, U1.ZOUT
  N3: WeMos_D1_Mini1.G, U1.COM
